# Fritzing sketch Receiver Circuits (saved by Fritzing 0.8.7b)
breadboards: 1

parts:
  Eleman1 = Arduino Uno (Rev3)
  Eleman2 = NRF24L01
  R1 = Resistor [tolerance=±5% resistance=220 package=THT]
  LED1 = LED - 5mm [color="Red (633nm)" package="5 mm [THT]"]

nets:
  N1: Eleman1.D8, Eleman2.CE
  N2: Eleman1.D11_PWM/MOSI, Eleman2.MOSI
  N3: Eleman1.D12/MISO, Eleman2.MISO
  N4: Eleman1.D13/SCK, Eleman2.SCK
  N5: Eleman1.D2, LED1.anode
  N6: Eleman1.D7, Eleman2.CSN
  5V: Eleman1.5V, Eleman2.VCC
  GND: Eleman1.GND, Eleman2.GND, R1.Pin_0
  N7: R1.Pin_1, LED1.cathode
